# Fritzing sketch Circuitdiagram (saved by Fritzing 0.9.3b)
breadboards: 1

parts:
  U1 = Sharp PC817 [package=THT]
  Raspberry_Pi_1 = Raspberry Pi 3 [part_number=RPI-3-V1.2]
  R2 = Resistor [tolerance=±5% resistance=220 package=THT]  # not connected
  R3 = Resistor [tolerance=±5% resistance=220 package=THT]
  VCC1 = Battery
  M1 = DC Motor
  Q1 = PNP-Transistor [package="TO92 [THT]"]
  R4 = Resistor [tolerance=±5% resistance=220 package=THT]
  U2 = Sharp PC817 [package=THT]
  R5 = Resistor [tolerance=±5% resistance=220 package=THT]
  Q2 = PNP-Transistor [package="TO92 [THT]"]
  R6 = Resistor [tolerance=±5% resistance=220 package=THT]
  IC1 = 4060 [package="DIP16 [THT]"]
  U7 = QRD1114 [package=qrd1114]
  L1 = Solenoid

nets:
  N1: U1.Pin_1, R3.Pin_0
  GND: U1.Pin_2, Raspberry_Pi_1.GND, U2.Pin_2, IC1.Q13, IC1.GND, U7.A
  N2: U1.Pin_4, VCC1.+, M1.pin_1, U2.Pin_4, U7.E, L1.pin2
  N3: U1.Pin_3, R4.Pin_0
  N4: Raspberry_Pi_1.GPIO10, IC1.Q6
  N5: Raspberry_Pi_1.GPIO9, IC1.Q4
  N6: Raspberry_Pi_1.GPIO11, IC1.Q5
  N7: Raspberry_Pi_1.GPIO8, IC1.Q3
  N8: Raspberry_Pi_1.5V, R3.Pin_1, R5.Pin_0, IC1.Q11, IC1.Q12
  N9: VCC1.-, Q1.E, Q2.E, U7.K
  N10: M1.pin_2, Q1.B
  N11: U2.Pin_1, R5.Pin_1
  N12: U2.Pin_3, R6.Pin_0
  N13: Q2.B, L1.pin1
  N14: Q2.C, R6.Pin_1
  N15: IC1.VDD, U7.C

notes:
  Raspberry Pi
  Flow Rate Sensor
  Solenoid Valve
  Air Pump (Motor)
  12V DC Power Source
